// Logisim project NSI_1ere_08_AlgebreDeBool_porte_not.circ as structural Verilog: 1 circuit, main circuit main
module main (
);

  wire not_1_out, undriven;

  not not_1 (not_1_out, undriven);

  // Notes on the sheet:
  //   E
  //   S
endmodule
