// Logisim project NSI_1ere_08_AlgebreDeBool_porte_or.circ as structural Verilog: 1 circuit, main circuit main
module main (
);

  wire or_1_out, undriven, undriven_2;

  or or_1 (or_1_out, undriven, undriven_2);

  // Notes on the sheet:
  //   E0
  //   E1
  //   S
endmodule
