// Logisim project NSI_1ere_08_AlgebreDeBool_decodeur.circ as structural Verilog: 1 circuit, main circuit main
module main (
);

  wire and_1_out, and_2_out, and_3_out, and_4_out, not_1_out, not_2_out, undriven, undriven_2;

  not not_1 (not_1_out, undriven);
  not not_2 (not_2_out, undriven_2);
  and and_1 (and_1_out, not_2_out, not_1_out);
  and and_2 (and_2_out, undriven, not_2_out);
  and and_3 (and_3_out, not_1_out, undriven_2);
  and and_4 (and_4_out, undriven, undriven_2);

  // Notes on the sheet:
  //   E0
  //   E1
  //   S0
  //   S1
  //   S2
  //   S3
endmodule
