// Logisim project NSI_1ere_08_AlgebreDeBool_porte_and.circ as structural Verilog: 1 circuit, main circuit main
module main (
);

  wire and_1_out, undriven, undriven_2;

  and and_1 (and_1_out, undriven, undriven_2);

  // Notes on the sheet:
  //   E0
  //   E1
  //   S
endmodule
