// Logisim project NSI_1ere_08_AlgebreDeBool_porte_xor.circ as structural Verilog: 1 circuit, main circuit main
module main (
);

  wire undriven, undriven_2, xor_1_out;

  xor xor_1 (xor_1_out, undriven, undriven_2);

  // Notes on the sheet:
  //   E0
  //   E1
  //   S
endmodule
